// Logisim project 2-BIT HALF ADDER USING NAND GATES.circ as structural Verilog: 1 circuit, main circuit main
module main (
  input  A,
  input  B,
  output sum_A_B,
  output carry_AB
);

  wire nand_1_out, nand_2_out, nand_3_out;

  nand nand_1 (nand_1_out, A, B);
  nand nand_2 (nand_2_out, A, nand_1_out);
  nand nand_3 (nand_3_out, nand_1_out, B);
  nand nand_4 (sum_A_B, nand_2_out, nand_3_out);
  nand nand_5 (carry_AB, nand_1_out, nand_1_out);
endmodule
