// Logisim project 2-BIT HALF ADDER USING NOR GATES.circ as structural Verilog: 1 circuit, main circuit main
module main (
  input  A,
  input  B,
  output sum_A_B,
  output carry_AB
);

  wire nor_1_out, nor_2_out, nor_3_out;

  nor nor_1 (nor_1_out, A, B);
  nor nor_2 (nor_2_out, A, A);
  nor nor_3 (nor_3_out, B, B);
  nor nor_4 (sum_A_B, nor_2_out, nor_3_out);
  nor nor_5 (carry_AB, sum_A_B, nor_1_out);
endmodule
