// Logisim project 3-BIT FULL ADDER USING NOR GATES.circ as structural Verilog: 1 circuit, main circuit main
module main (
  input  A,
  input  B,
  input  Cin,
  output x_carry,
  output out_5
);

  wire nor_1_out, nor_2_out, nor_3_out, nor_4_out, nor_5_out, nor_6_out, nor_7_out, nor_8_out, nor_9_out,
       nor_10_out;

  nor nor_1 (nor_1_out, A, A);
  nor nor_2 (nor_2_out, A, B);
  nor nor_3 (nor_3_out, B, B);
  nor nor_4 (nor_4_out, nor_1_out, nor_3_out);
  nor nor_5 (nor_5_out, nor_4_out, nor_2_out);
  nor nor_6 (nor_6_out, nor_5_out, nor_5_out);
  nor nor_7 (nor_7_out, nor_5_out, Cin);
  nor nor_8 (nor_8_out, Cin, Cin);
  nor nor_9 (nor_9_out, nor_6_out, nor_8_out);
  nor nor_10 (nor_10_out, nor_4_out, nor_9_out);
  nor nor_11 (out_5, nor_9_out, nor_7_out);
  nor nor_12 (x_carry, nor_10_out, nor_10_out);

  // Notes on the sheet:
  //   y=sum
endmodule
