// Logisim project 4bitcarry.circ as structural Verilog: 1 circuit, main circuit main
module main (
  input  B3,
  input  A3,
  input  B2,
  input  A2,
  input  B1,
  input  A1,
  input  B0,
  input  A0,
  output C4,
  output C3,
  output out_11,
  output C1
);

  wire and_1_out, and_2_out, and_3_out, and_4_out, and_5_out, and_6_out, and_7_out, and_8_out, and_9_out,
       and_10_out, G0_out, G1_out, G2_out, G3_out, P1_out, P2_out, P3_out, undriven;

  xor P3 (P3_out, B3, A3);
  and G3 (G3_out, B3, A3);
  xor P2 (P2_out, B2, A2);
  and G2 (G2_out, B2, A2);
  xor P1 (P1_out, B1, A1);
  and G1 (G1_out, B1, A1);
  xor P0 (P1_out, B0, A0);
  and G0 (G0_out, B0, A0);
  and and_1 (and_1_out, P2_out, P1_out, P1_out, P3_out, undriven);
  and and_2 (and_2_out, G1_out, P2_out, P3_out);
  and and_3 (and_3_out, G0_out, P1_out, P2_out, P3_out, P3_out);
  and and_4 (and_4_out, P3_out, G2_out);
  and and_5 (and_5_out, G1_out, P2_out);
  and and_6 (and_6_out, P1_out, G0_out, P2_out);
  and and_7 (and_7_out, P1_out, P1_out, P2_out, undriven);
  and and_8 (and_8_out, P1_out, G0_out);
  and and_9 (and_9_out, P1_out, P1_out, undriven);
  and and_10 (and_10_out, P1_out, P1_out, undriven);
  or or_1 (C4, and_1_out, and_2_out, and_3_out, and_4_out, G3_out);
  or or_2 (C3, and_5_out, and_6_out, and_7_out, G2_out);
  or or_3 (out_11, and_8_out, and_9_out, G1_out);
  or or_4 (C1, and_10_out, G0_out);

  // Notes on the sheet:
  //   G1
  //   C0
  //   P0
  //   G0
  //   P1
  //   P0
  //   P2P1P0C0
  //   G2
  //   P1G0
  //   C0P0P1P2P3
  //   G1P3P2
  //   G0P3P2P1
  //   P3G2
  //   P2G1
  //   P2P1G0
  //   P1P0C0
  //   P0 C0
  //   G0
  //   G3
  //   G2
  //   G1
  //   C2
endmodule
