// Logisim project HALF ADDER.circ as structural Verilog: 1 circuit, main circuit main
module main (
  input  A,
  input  B,
  output sum_A_B,
  output carry_AB
);

  xor xor_1 (sum_A_B, A, B);
  and and_1 (carry_AB, A, B);
endmodule
