// Logisim project halfadder.circ as structural Verilog: 1 circuit, main circuit main
module main (
  input  A,
  input  B,
  output sum_a_b,
  output carry_ab
);

  xor xor_1 (sum_a_b, A, B);
  and and_1 (carry_ab, A, B);
endmodule
